# Fritzing sketch CalendarHouse (saved by Fritzing 1.0.4)
breadboards: 2

parts:
  AZDelivery_ESP32_V4_DevKit = MH-ET LIVE ESP32 DEVKIT 38 pins
  R1 = Resistor [tolerance=±5% power=0.25W resistance=22k package=THT]
  R2 = Resistor [tolerance=±5% power=0.25W resistance=22k package=THT]
  R3 = Resistor [tolerance=±5% power=0.25W resistance=4.7k package=THT]
  R4 = Resistor [tolerance=±5% power=0.25W resistance=4.7k package=THT]
  Amplifier = PAM8403 Stereo Amplifier with Volume Control [part_number="AZDelivery PAM"]
  Speaker_Left = SPEAKER [package=pcb_mount_speaker]
  Speaker_Right = SPEAKER [package=pcb_mount_speaker]
  C2 = Electrolytic Capacitor [capacitance=1mF voltage=10V package="100 mil [THT, electrolytic]"]
  TLC5947 = 24-Channel 12-bit PWM LED Driver - SPI [part_number=1429]
  A1 = PFC8575 module
  A2 = PFC8575 module
  U1 = A3144 Hall Effect Sensor. [package="UA [THT]"]
  R5 = Resistor [tolerance=±5% power=0.25W resistance=10k package=THT]
  U2 = A3144 Hall Effect Sensor. [package="UA [THT]"]
  R6 = Resistor [tolerance=±5% power=0.25W resistance=10k package=THT]
  LED1 = LED - 5mm [color="White (6500K)" current=0.030A package="5 mm [THT]"]
  LED2 = LED - 5mm [color="White (6500K)" current=0.030A package="5 mm [THT]"]
  R8 = Resistor [tolerance=±5% power=0.25W resistance=100k package=THT]
  R9 = Resistor [tolerance=±5% power=0.25W resistance=100k package=THT]
  Q1 = Basic FET N-Channel [part_number=2N7000 package="TO220 [THT]"]
  R10 = Resistor [tolerance=±5% power=0.25W resistance=1k package=THT]
  M2 = MT3608 Module
  Q2 = Basic FET N-Channel [part_number=2N7000 package="TO220 [THT]"]
  R11 = Resistor [tolerance=±5% power=0.25W resistance=1k package=THT]
  A3 = Micro SD card reader

nets:
  3V3: AZDelivery_ESP32_V4_DevKit.3V3, A3.Pin_1
  HALL EN: AZDelivery_ESP32_V4_DevKit.IO32, Q1.drain, R10.Pin_1
  N1: AZDelivery_ESP32_V4_DevKit.IO33, Q2.drain, R11.Pin_1
  I2S R: AZDelivery_ESP32_V4_DevKit.IO25, R2.Pin_0
  I2S L: AZDelivery_ESP32_V4_DevKit.IO26, R1.Pin_0
  HSPI CLK: AZDelivery_ESP32_V4_DevKit.IO14, A3.Pin_4
  HSPI MISO: AZDelivery_ESP32_V4_DevKit.IO12, A3.Pin_5
  GND: AZDelivery_ESP32_V4_DevKit.GND#58, C2.-, Q2.gate, R11.Pin_0, A3.Pin_6
  HSPI MOSI: AZDelivery_ESP32_V4_DevKit.IO13, A3.Pin_3
  5V: AZDelivery_ESP32_V4_DevKit.5V, Amplifier.POWER+, C2.+, A1.Pin_22, A2.Pin_22, U1.+Vsupply, R5.Pin_0, U2.+Vsupply, R6.Pin_0, R8.Pin_0, R9.Pin_0, M2.pin2
  VSPI MOSI: AZDelivery_ESP32_V4_DevKit.IO23, TLC5947.DIN
  I2C SCL: AZDelivery_ESP32_V4_DevKit.IO22, A1.Pin_24, A2.Pin_24, R9.Pin_1
  I2C SDA: AZDelivery_ESP32_V4_DevKit.IO21, A1.Pin_23, A2.Pin_23, R8.Pin_1
  VSPI SCLK: AZDelivery_ESP32_V4_DevKit.IO18, TLC5947.CLK
  VSPI CS: AZDelivery_ESP32_V4_DevKit.IO5, TLC5947.LAT
  HSPI CS: AZDelivery_ESP32_V4_DevKit.IO15, A3.Pin_2
  N2: R1.Pin_1, R3.Pin_0, Amplifier.INPUTL
  N3: R2.Pin_1, R4.Pin_0, Amplifier.INPUTR
  EXT GND: R3.Pin_1, R4.Pin_1, Amplifier.POWER-, TLC5947.GND, Q1.gate, R10.Pin_0, M2.pin1, M2.pin4, Q2.source
  N4: Amplifier.ROUT-, Speaker_Right.+
  N5: Amplifier.ROUT+, Speaker_Right.-
  N6: Amplifier.LOUT+, Speaker_Left.-
  N7: Amplifier.LOUT-, Speaker_Left.+
  12V: TLC5947.+24V, LED1.anode, LED2.anode, M2.pin3
  N8: TLC5947.PWM0, LED1.cathode
  N9: TLC5947.PWM3, LED2.cathode
  N10: A1.Pin_3, U1.Out, R5.Pin_1
  GND_2: A1.Pin_20, A1.Pin_21, A2.Pin_20, A2.Pin_21, U1.GND, U2.GND, Q1.source
  N11: A2.Pin_4, U2.Out, R6.Pin_1

notes:
  5V -> 12V
  24 LEDs driven by PWM
  General External Module Switch
  Hall Sensors Switch
  24 Hall Sensors
  Power provided via USB
  From Powerbank to ESP32 Module
  Music/Story Player
  24 LEDs driver
  I2C pull-ups
  24 hall sensors
  Hall sensors poll activation
  Stereo music player (I2S)
  Modules Power Switch
  What do these R do??
  SD Card Reader
  18-11-2024
  Rev A0.3
  Calendar House, A0.3

custom parts:
  MH-ET LIVE ESP32 DEVKIT 38 pins: http://mh.nodebb.com/topic/2/mh-et-live-esp32-devkit
  PAM8403 Stereo Amplifier with Volume Control: PAM8403 stereo amplifier module with volume control Descriptive words Links: PAM8403 product datasheet
  24-Channel 12-bit PWM LED Driver - SPI: This breakout board for the TLC5947 PWM driver chip can control 24 separate channels of 12-bit PWM output. Designed (and ideal) for LED control, this board is NOT good for driving servos. Only three "SPI" pins are required to send data (our Arduino library shows how to to use any digital microcontroller pins). Best of all, the design is completely chainable. As long as there's enough power for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
  PFC8575 module: PCF8575 IO Expander Module I2C To 16IO.
  A3144 Hall Effect Sensor.: Allegro A3144 hall effect switch for high temperature operation.
  MT3608 Module: MT3608 Boost Converter Module Links: Aerosemi MT3608 2A Step Up Converter datasheet
  Micro SD card reader: Micro SD card reader.
